# Fritzing sketch diagram (saved by Fritzing 0.9.3b)
breadboards: 2

parts:
  Part1 = Arduino Uno (Rev3)
  hc-sr1 = hc-sr04
  Part2 = Bluetooth HC-05 Macho

nets:
  N1: Part1.D2, Part2.TXD
  N2: Part1.D3_PWM, Part2.RXD
  N3: Part1.D5_PWM, hc-sr1.Trig
  N4: Part1.D6_PWM, hc-sr1.Echo
  VCC: Part1.5V, hc-sr1.VCC, Part2.VCC
  GND: Part1.GND, hc-sr1.GND, Part2.GND
